# Fritzing sketch Programador_attiny85 (saved by Fritzing 0.8.5b)
circuit board: 2.73977cm x 5.87552cm

parts:
  Parte1 = Arduino Uno (Rev3)
  ZOCALO = attiny85 [package=dip]
  10uF/16V = Electrolytic Capacitor [capacitance=10µF voltage=16V package="100 mil [THT, electrolytic]"]
  LED = LED - 5mm [color="Red (633nm)" package="5 mm [THT]"]
  470 = Resistor [tolerance=±5% resistance=470 package=THT]

nets:
  N1: Parte1.D10_PWM/SS, ZOCALO.Pin_1
  N2: Parte1.D11_PWM/MOSI, ZOCALO.Pin_5
  N3: Parte1.D12/MISO, ZOCALO.Pin_6
  N4: Parte1.D13/SCK, ZOCALO.Pin_7
  N5: Parte1.GND, ZOCALO.Pin_4, 10uF/16V.-, LED.cathode
  N6: Parte1.RESET, 10uF/16V.+
  N7: Parte1.5V, ZOCALO.Pin_8, 470.Pin_1
  N8: LED.anode, 470.Pin_0

notes:
  10uF / 16V
  LED
  470
